# Fritzing sketch Circuit_Diagram_ESPWROOM32 (saved by Fritzing 0.9.9b)
breadboards: 1

parts:
  Componente1 = BME280 Breakout
  ZS-042_RTC1 = ZS-042 RTC Module
  Grove1 = Grove OLED 128x96
  RE2 = KY-040 Rotary encoder [package=THT]
  microSD1 = MicroSD Card Module
  TP1 = TP4056 [chip_label=TP4056 package="DIP (Dual Inline) [THT]"]
  BAT1 = Battery Holders [package=battery-aa-kit]
  CPU1 = NodeMCU WROOM ESP 32
  Part2 = Solar Cell

nets:
  GND: Componente1.GND, ZS-042_RTC1.GND, Grove1.GND, RE2.GND, microSD1.GND, TP1.pin6, CPU1.pin_15
  VCC: Componente1.3.3V, ZS-042_RTC1.VCC, Grove1.VCC, RE2.Vcc, microSD1.VCC, TP1.pin3, CPU1.pin_16, CPU1.pin_17
  N1: Componente1.SDI/SDA, Grove1.SDA
  N2: Componente1.SCK/SCL, ZS-042_RTC1.SCL, Grove1.SCL, CPU1.pin_30
  N3: ZS-042_RTC1.SDA, CPU1.pin_27
  N4: RE2.SW, microSD1.CS, CPU1.pin_8, CPU1.pin_24, CPU1.pin_28
  N5: RE2.DT, microSD1.SCK, CPU1.pin_9, CPU1.pin_25
  N6: RE2.CLK, CPU1.pin_10
  N7: microSD1.MISO, CPU1.pin_26
  N8: microSD1.MOSI, CPU1.pin_31
  N9: TP1.pin1, Part2.+
  N10: TP1.pin2, Part2.-
  N11: TP1.pin4, BAT1.+
  N12: TP1.pin5, BAT1.-

custom parts:
  KY-040 Rotary encoder: KY-040 Rotary Encoder with switch on breakout borad from AZ Delivery
  TP4056: A DIP stand-in part for whatever IC you want. With 6 pins on a 300mil dual inline package (DIP) footprint.
  NodeMCU WROOM ESP 32: 30 pol Development Kit
